# Fritzing sketch Untitled Sketch 4 (saved by Fritzing 1.0.5)

parts:
  esp1 = ESP32 DevKitc V4
  TP1 = TP4056 [chip_label=TP4056 package="DIP (Dual Inline) [THT]"]
  C1 = Electrolytic Capacitor [capacitance=1000µF voltage=35V package="300 mil [THT, electrolytic]"]
  U1 = Mini-360 DC-DC Buck converter [package=THT]
  J1 = Piezo Speaker
  BAT1 = Battery Holders [package=lipo-1100mAh]
  8x8_LED_Modul_mit_MAX1 = 8x8 LED Modul mit MAX7219 [package=THT]

nets:
  N1: esp1.IO5, 8x8_LED_Modul_mit_MAX1.CS_Eingang
  N2: esp1.IO18, 8x8_LED_Modul_mit_MAX1.CLK_Eingang
  N3: esp1.GND#12, C1.-, U1.OUT-, 8x8_LED_Modul_mit_MAX1.GND_Eingang
  N4: esp1.IO23, 8x8_LED_Modul_mit_MAX1.DIN_Eingang
  N5: esp1.IO34, J1.pin2
  N6: esp1.GND#32, J1.pin1
  N7: esp1.5V, C1.+, U1.OUT+, 8x8_LED_Modul_mit_MAX1.VCC_Eingang
  N8: TP1.pin3, U1.IN+
  N9: TP1.pin4, BAT1.+
  N10: TP1.pin5, BAT1.-
  N11: TP1.pin6, U1.IN-

custom parts:
  ESP32 DevKitc V4: ESP32-DevKitC board with ESP32-WROOM-32 module. ESP32-DevKitC V4 is a small-sized ESP32-based development board produced by Espressif. Most of the pins on the ESP module are broken out to the pin headers on the board. The pins D0, D1, D2, D3, CMD and CLK are used internally for communication between ESP32 and SPI flash memory. They are grouped on both sides near the USB connector. Avoid using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
  TP4056: A DIP stand-in part for whatever IC you want. With 6 pins on a 300mil dual inline package (DIP) footprint.
  Mini-360 DC-DC Buck converter: Mini-360 DC-DC Buck converter. Tiny buck step down voltage converter, input voltage 4.75 to 23V output 1 to 17V adjustable. Available from ebay and the like.
